# Fritzing sketch Circuit (saved by Fritzing 0.9.3b)
circuit board: 8.46667cm x 5.64444cm
breadboards: 1

parts:
  ESP8266 = IC, DIP package, 20 pins [chip_label=IC]
  RFID = IC, SIP package, 8 pins [chip_label=IC]
  R1 = Resistor [tolerance=±5% resistance=220 package=THT]
  buzzer = Piezo Speaker
  LED1 = LED - 5mm [color="Red (633nm)" package="5 mm [THT]"]

nets:
  N1: ESP8266.pin1, RFID.pin8
  N2: ESP8266.pin3, RFID.pin2
  N3: ESP8266.pin4, RFID.pin4
  N4: ESP8266.pin5, RFID.pin3
  N5: ESP8266.pin7, RFID.pin1
  N6: ESP8266.pin8, RFID.pin7
  N7: ESP8266.pin9, RFID.pin6
  N8: ESP8266.pin12, R1.Pin_0
  N9: ESP8266.pin13, LED1.anode
  N10: ESP8266.pin16, buzzer.pin2
  N11: ESP8266.pin20, buzzer.pin1
  N12: R1.Pin_1, LED1.cathode
